# Fritzing sketch Common Cathode RGB (saved by Fritzing 0.9.3b)

parts:
  R1 = Resistor [tolerance=±5% resistance=220 package=THT]
  R2 = Resistor [tolerance=±5% resistance=220 package=THT]
  R3 = Resistor [tolerance=±5% resistance=220 package=THT]
  Part1 = Arduino Uno (Rev3)
  LED1 = RGB LED (com. cathode, rbg) [package="5 mm [THT]"]

nets:
  N1: R1.Pin_0, Part1.D2
  N2: R2.Pin_0, Part1.D0/RX
  N3: R3.Pin_0, Part1.D1/TX
  N4: Part1.GND, LED1.common_cathode
